// Digital circuit 4bit_CPU (1).dig as structural Verilog
module _4bit_CPU__1 (
  input  CK,
  input  [3:0] D,
  input  [1:0] SP,
  input  [1:0] SP_2,
  input  [1:0] SP_3,
  input  [1:0] SP_4,
  input  [3:0] Address,
  input  I,
  input  L,
  input  [3:0] C1,
  input  [3:0] C2,
  input  [3:0] C3,
  input  [3:0] A,
  input  [3:0] B,
  input  [3:0] Clear,
  output [3:0] CU,
  output [3:0] AO,
  output [3:0] BO
);

  wire [3:0] Program_Counter_o, ram__1_1_output;

  Program_Counter Program_Counter (.CK(CK), .I(I), .L(L), .D(Address), .O(Program_Counter_o));
  RAM__1 ram__1_1 (.Data(D), .SP(SP), .A(Program_Counter_o), .CK(CK), .Clear(Clear), .Output(ram__1_1_output));
  IR Instruction_Register (.SP(SP_2), .D(ram__1_1_output), .CK(CK), .C(C1), .O(CU));
  Register Register_A (.CK(CK), .C(C2), .SP(SP_3), .D(A), .O(AO));
  Register Register_B (.CK(CK), .C(C3), .SP(SP_4), .D(B), .O(BO));
endmodule
