// Digital circuit RAM (1).dig as structural Verilog
module RAM__1 (
  input  [3:0] Data,
  input  [1:0] SP,
  input  [3:0] A,
  input  CK,
  input  [3:0] Clear,
  output [3:0] Output
);

  wire [1:0] demultiplexer_1_out_0, demultiplexer_1_out_1, demultiplexer_1_out_2, demultiplexer_1_out_3,
       demultiplexer_1_out_4, demultiplexer_1_out_5, demultiplexer_1_out_6, demultiplexer_1_out_7,
       demultiplexer_1_out_8, demultiplexer_1_out_9, demultiplexer_1_out_10, demultiplexer_1_out_11,
       demultiplexer_1_out_12, demultiplexer_1_out_13, demultiplexer_1_out_14, demultiplexer_1_out_15;
  wire [3:0] Address_0_o, Address_1_o, Address_2_o, Address_3_o, Address_4_o, Address_5_o, Address_6_o,
       Address_7_o, Address_8_o, Address_9_o, Address_10_o, Address_11_o, Address_12_o, Address_13_o,
       Address_14_o, Address_15_o;

  Demultiplexer #(.Selector_Bits(4), .Bits(2)) demultiplexer_1 (
    .sel(A), .in(SP), .out_0(demultiplexer_1_out_0), .out_1(demultiplexer_1_out_1),
    .out_2(demultiplexer_1_out_2), .out_3(demultiplexer_1_out_3), .out_4(demultiplexer_1_out_4),
    .out_5(demultiplexer_1_out_5), .out_6(demultiplexer_1_out_6), .out_7(demultiplexer_1_out_7),
    .out_8(demultiplexer_1_out_8), .out_9(demultiplexer_1_out_9), .out_10(demultiplexer_1_out_10),
    .out_11(demultiplexer_1_out_11), .out_12(demultiplexer_1_out_12), .out_13(demultiplexer_1_out_13),
    .out_14(demultiplexer_1_out_14), .out_15(demultiplexer_1_out_15));
  Register Address_0 (.CK(CK), .C(Clear), .SP(demultiplexer_1_out_0), .D(Data), .O(Address_0_o));
  Register Address_1 (.CK(CK), .C(Clear), .SP(demultiplexer_1_out_1), .D(Data), .O(Address_1_o));
  Register Address_2 (.CK(CK), .C(Clear), .SP(demultiplexer_1_out_2), .D(Data), .O(Address_2_o));
  Register Address_3 (.CK(CK), .C(Clear), .SP(demultiplexer_1_out_3), .D(Data), .O(Address_3_o));
  Register Address_4 (.CK(CK), .C(Clear), .SP(demultiplexer_1_out_4), .D(Data), .O(Address_4_o));
  Register Address_5 (.CK(CK), .C(Clear), .SP(demultiplexer_1_out_5), .D(Data), .O(Address_5_o));
  Register Address_6 (.CK(CK), .C(Clear), .SP(demultiplexer_1_out_6), .D(Data), .O(Address_6_o));
  Register Address_7 (.CK(CK), .C(Clear), .SP(demultiplexer_1_out_7), .D(Data), .O(Address_7_o));
  Register Address_8 (.CK(CK), .C(Clear), .SP(demultiplexer_1_out_8), .D(Data), .O(Address_8_o));
  Register Address_9 (.CK(CK), .C(Clear), .SP(demultiplexer_1_out_9), .D(Data), .O(Address_9_o));
  Register Address_10 (.CK(CK), .C(Clear), .SP(demultiplexer_1_out_10), .D(Data), .O(Address_10_o));
  Register Address_11 (.CK(CK), .C(Clear), .SP(demultiplexer_1_out_11), .D(Data), .O(Address_11_o));
  Register Address_12 (.CK(CK), .C(Clear), .SP(demultiplexer_1_out_12), .D(Data), .O(Address_12_o));
  Register Address_13 (.CK(CK), .C(Clear), .SP(demultiplexer_1_out_13), .D(Data), .O(Address_13_o));
  Register Address_14 (.CK(CK), .C(Clear), .SP(demultiplexer_1_out_14), .D(Data), .O(Address_14_o));
  Register Address_15 (.CK(CK), .C(Clear), .SP(demultiplexer_1_out_15), .D(Data), .O(Address_15_o));
  Multiplexer #(.Selector_Bits(4), .Bits(4)) multiplexer_1 (
    .sel(A), .in_0(Address_0_o), .in_1(Address_1_o), .in_2(Address_2_o), .in_3(Address_3_o),
    .in_4(Address_4_o), .in_5(Address_5_o), .in_6(Address_6_o), .in_7(Address_7_o), .in_8(Address_8_o),
    .in_9(Address_9_o), .in_10(Address_10_o), .in_11(Address_11_o), .in_12(Address_12_o),
    .in_13(Address_13_o), .in_14(Address_14_o), .in_15(Address_15_o), .out(Output));
endmodule
