// Digital circuit Register.dig as structural Verilog
module Register (
  input  CK,
  input  [3:0] C,
  input  [1:0] SP,
  input  [3:0] D,
  output [3:0] O
);

  wire [3:0] multiplexer_1_out;

  Multiplexer #(.Selector_Bits(2), .Bits(4)) multiplexer_1 (
    .sel(SP), .in_0(C), .in_1(D), .in_2(O), .in_3(4'b0000), .out(multiplexer_1_out));
  D_FF d_ff_1 (.D(multiplexer_1_out[3]), .C(CK), .Q(O[3]));  // open: nQ
  D_FF d_ff_2 (.D(multiplexer_1_out[2]), .C(CK), .Q(O[2]));  // open: nQ
  D_FF d_ff_3 (.D(multiplexer_1_out[1]), .C(CK), .Q(O[1]));  // open: nQ
  D_FF d_ff_4 (.D(multiplexer_1_out[0]), .C(CK), .Q(O[0]));  // open: nQ
endmodule
